# Fritzing sketch designe (saved by Fritzing 0.9.3b)

parts:
  Part1 = Arduino Uno (Rev3)
  GSM_SIM_GPSR_SMS_SIM900_SIM1 = SIM800L [package=THT]
  M1 = RioRand LM2596
  S2 = H-Bridge with L298N
  M2 = DC Motor
  M3 = DC Motor
  M4 = DC Motor
  M5 = DC Motor
  S3 = KY-026
  S4 = KY-026
  S5 = KY-026
  VCC1 = 4 x AAA Battery Mount
  J1 = Piezo Speaker
  Mod1 = KY-019 5V Relay Module [package="Breakout board"]
  J2 = Basic Servo
  M6 = DC Motor
  D1 = Rectifier Diode [part_number=1N4001 package="300 mil [THT]"]  # not connected

nets:
  N1: Part1.A0, S4.pin4
  N2: Part1.A1, S5.pin4
  N3: Part1.A2, S3.pin4
  N4: Part1.D8, S2.IN2
  N5: Part1.D9_PWM, S2.IN1
  N6: Part1.D10_PWM/SS, J2.pulse
  N7: Part1.D11_PWM/MOSI, S2.ENA
  N8: Part1.D13/SCK, J1.pin2
  GND: Part1.GND, S2.GND
  N9: Part1.D2, GSM_SIM_GPSR_SMS_SIM900_SIM1.SIM_RXD
  N10: Part1.D3_PWM, GSM_SIM_GPSR_SMS_SIM900_SIM1.SIM_TXD
  N11: Part1.D4, Mod1.S
  N12: Part1.D5_PWM, S2.ENB
  N13: Part1.D6_PWM, S2.IN4
  N14: Part1.D7, S2.IN3
  N15: Part1.5V, M1.Pin_3
  N16: M1.Pin_1, VCC1.+
  N17: M1.Pin_2, VCC1.-
  N18: S2.M1-01, M4.pin_1, M5.pin_1
  N19: S2.M1-02, M4.pin_2, M5.pin_2
  N20: S2.M2-01, M2.pin_1, M3.pin_1
  N21: S2.M2-02, M2.pin_2, M3.pin_2
  N22: Mod1.NO, M6.pin_1

notes:
  Right
  center
  left
  in-
  in+

custom parts:
  H-Bridge with L298N: h-bridge
  KY-026: ky-026 flame sensor module
  KY-019 5V Relay Module: KY-019 5V Relay module, used to control AC circuits. (Special thanks to vanepp for fixing the PCB holes and other errors)
